// Logisim project Trabalho.circ as structural Verilog: 12 circuits, main circuit main
module main (
);


  // Notes on the sheet:
  //   e depois use aquele circuito para construir sua calculadora.
  //   Este projeto foi fornecido apenas para que você altere o circuito alu-8-bits,
endmodule

module alu_8_bits (
  input  [7:0] A,
  input  [7:0] B,
  input  [2:0] OP,
  input  Cin,
  output [7:0] s,
  output c,
  output z
);
endmodule

module somador_2_bits (
  input  A,
  input  B,
  input  Qin,
  output S,
  output Qout
);

  wire and_1_out, and_2_out, and_3_out, and_4_out, and_5_out, and_6_out, and_7_out, not_1_out, not_2_out,
       not_3_out, not_4_out, not_5_out, not_6_out;

  not not_1 (not_1_out, A);
  not not_2 (not_2_out, B);
  not not_3 (not_3_out, A);
  not not_4 (not_4_out, Qin);
  not not_5 (not_5_out, B);
  not not_6 (not_6_out, Qin);
  and and_1 (and_1_out, B, Qin);
  and and_2 (and_2_out, A, Qin);
  and and_3 (and_3_out, A, B);
  and and_4 (and_4_out, not_1_out, not_2_out, Qin);
  and and_5 (and_5_out, not_3_out, B, not_4_out);
  and and_6 (and_6_out, A, not_5_out, not_6_out);
  and and_7 (and_7_out, A, B, Qin);
  or or_1 (Qout, and_1_out, and_2_out, and_3_out);
  or or_2 (S, and_4_out, and_5_out, and_6_out, and_7_out);
endmodule

module somador_8_bits (
  input  [7:0] A,
  input  [7:0] B,
  output [7:0] S,
  output Qout
);

  wire somador_2_bits_2_qout, somador_2_bits_3_qout, somador_2_bits_4_qout, somador_2_bits_5_qout,
       somador_2_bits_6_qout, somador_2_bits_7_qout, somador_2_bits_8_qout;

  somador_2_bits somador_2_bits_1 (.A(A[7]), .B(B[7]), .Qin(somador_2_bits_2_qout), .S(S[7]), .Qout(Qout));
  somador_2_bits somador_2_bits_2 (
    .A(A[6]), .B(B[6]), .Qin(somador_2_bits_3_qout), .S(S[6]), .Qout(somador_2_bits_2_qout));
  somador_2_bits somador_2_bits_3 (
    .A(A[5]), .B(B[5]), .Qin(somador_2_bits_4_qout), .S(S[5]), .Qout(somador_2_bits_3_qout));
  somador_2_bits somador_2_bits_4 (
    .A(A[4]), .B(B[4]), .Qin(somador_2_bits_5_qout), .S(S[4]), .Qout(somador_2_bits_4_qout));
  somador_2_bits somador_2_bits_5 (
    .A(A[3]), .B(B[3]), .Qin(somador_2_bits_6_qout), .S(S[3]), .Qout(somador_2_bits_5_qout));
  somador_2_bits somador_2_bits_6 (
    .A(A[2]), .B(B[2]), .Qin(somador_2_bits_7_qout), .S(S[2]), .Qout(somador_2_bits_6_qout));
  somador_2_bits somador_2_bits_7 (
    .A(A[1]), .B(B[1]), .Qin(somador_2_bits_8_qout), .S(S[1]), .Qout(somador_2_bits_7_qout));
  somador_2_bits somador_2_bits_8 (.A(A[0]), .B(B[0]), .Qin(1'b0), .S(S[0]), .Qout(somador_2_bits_8_qout));
endmodule

module XOR_2_bits (
  input  A,
  input  B,
  output S
);

  wire and_1_out, and_2_out, not_1_out, not_2_out;

  not not_1 (not_1_out, A);
  not not_2 (not_2_out, B);
  and and_1 (and_1_out, not_1_out, B);
  and and_2 (and_2_out, A, not_2_out);
  or or_1 (S, and_1_out, and_2_out);
endmodule

module XOR_8_bits (
  input  [7:0] A,
  input  [7:0] B,
  output [7:0] S
);

  XOR_2_bits xor_2_bits_1 (.A(A[7]), .B(B[7]), .S(S[7]));
  XOR_2_bits xor_2_bits_2 (.A(A[6]), .B(B[6]), .S(S[6]));
  XOR_2_bits xor_2_bits_3 (.A(A[5]), .B(B[5]), .S(S[5]));
  XOR_2_bits xor_2_bits_4 (.A(A[4]), .B(B[4]), .S(S[4]));
  XOR_2_bits xor_2_bits_5 (.A(A[3]), .B(B[3]), .S(S[3]));
  XOR_2_bits xor_2_bits_6 (.A(A[2]), .B(B[2]), .S(S[2]));
  XOR_2_bits xor_2_bits_7 (.A(A[1]), .B(B[1]), .S(S[1]));
  XOR_2_bits xor_2_bits_8 (.A(A[0]), .B(B[0]), .S(S[0]));
endmodule

module AND_8_bits (
  input  [7:0] A,
  input  [7:0] B,
  output [7:0] S
);

  and and_1 (S[7], A[7], B[7]);
  and and_2 (S[6], A[6], B[6]);
  and and_3 (S[5], A[5], B[5]);
  and and_4 (S[3], A[3], B[3]);
  and and_5 (S[4], A[4], B[4]);
  and and_6 (S[2], A[2], B[2]);
  and and_7 (S[1], A[1], B[1]);
  and and_8 (S[0], A[0], B[0]);
endmodule

module OR_8_bits (
  input  [7:0] A,
  input  [7:0] B,
  output [7:0] S
);

  or or_1 (S[7], A[7], B[7]);
  or or_2 (S[6], A[6], B[6]);
  or or_3 (S[5], A[5], B[5]);
  or or_4 (S[4], A[4], B[4]);
  or or_5 (S[3], A[3], B[3]);
  or or_6 (S[2], A[2], B[2]);
  or or_7 (S[1], A[1], B[1]);
  or or_8 (S[0], A[0], B[0]);
endmodule

module Shift_Left_8_bits (
  input  [7:0] B,
  output [7:0] S
);


  assign S = {B[6:0], 1'b0};
endmodule

module Shift_Right_8_bits (
  input  [7:0] B,
  output [7:0] S
);


  assign S = {1'b0, B[7:1]};
endmodule

module Mux_1_bit (
  input  A,
  input  B,
  input  Mux,
  output S
);

  wire and_1_out, and_2_out, not_1_out;

  not not_1 (not_1_out, Mux);
  and and_1 (and_1_out, B, Mux);
  and and_2 (and_2_out, A, not_1_out);
  or or_1 (S, and_1_out, and_2_out);
endmodule

module Mux_3_bits (
  input  [2:0] MUX,
  input  [7:0] A,
  input  [7:0] B
);
endmodule
